// Logisim project alu.circ as structural Verilog: 1 circuit, main circuit alu
module alu (
  input  [31:0] A,
  input  [31:0] B,
  input  [3:0] ALUSel,
  output [31:0] Result
);

  wire xor_4_out;
  wire [0:0] slt1;
  wire [31:0] add, adder_2_out, adder_3_out, and1, divider_2_out, divu, mul, mulh, mulhu, multiplexer_2_out,
       multiplexer_3_out, multiplier_3_out, multiplier_4_cout, or1, remu, sll1, sra1, srl1, sub, vaddh, xor1,
       xor_2_out, xor_3_out, xor_5_out;

  Adder #(.width(32)) adder_1 (.a(A), .b(B), .out(add));  // open: cin, cout
  assign and1 = A & B;  // AND_Gate and_1, 32 bits wide
  assign or1 = A | B;  // OR_Gate or_1, 32 bits wide
  assign xor1 = A ^ B;  // XOR_Gate xor_1, 32 bits wide
  Shifter #(.width(32), .shift("lr")) shifter_1 (.in(A), .\dist (B[4:0]), .out(srl1));
  Shifter #(.width(32), .shift("ar")) shifter_2 (.in(A), .\dist (B[4:0]), .out(sra1));
  Shifter #(.width(32)) shifter_3 (.in(A), .\dist (B[4:0]), .out(sll1));
  Comparator #(.width(32)) comparator_1 (.a(A), .b(B), .lt(slt1[0]));  // open: gt, eq
  Divider #(.width(32)) divider_1 (.a(A), .b(B), .out(divu));  // open: upper, rem
  Divider #(.width(32)) divider_2 (.a(A), .b(B), .out(divider_2_out));  // open: upper, rem
  Multiplier #(.width(32)) multiplier_1 (.a(A), .b(B), .out(mul));  // open: cin, cout
  Multiplier #(.width(32)) multiplier_2 (.a(A), .b(B), .cout(mulhu));  // open: out, cin
  Subtractor #(.width(32)) subtractor_1 (.a(A), .b(B), .out(sub));  // open: bin, bout
  Multiplier #(.width(32)) multiplier_3 (.a(divider_2_out), .b(B), .out(multiplier_3_out));  // open: cin, cout
  Subtractor #(.width(32)) subtractor_2 (.a(A), .b(multiplier_3_out), .out(remu));  // open: bin, bout
  Multiplexer #(.select(4), .width(32), .enable("false")) multiplexer_1 (
    .in0(add), .in1(and1), .in2(or1), .in3(xor1), .in4(srl1), .in5(sra1), .in6(sll1),
    .in7({{31{1'b0}}, slt1[0]}), .in8(divu), .in9(remu), .in10(mul), .in11(mulhu), .in12(sub), .in13(B),
    .in14(mulh), .in15(vaddh), .out(Result), .sel(ALUSel));
  assign xor_2_out = A ^ {32{1'b1}};  // XOR_Gate xor_2, 32 bits wide
  assign xor_3_out = B ^ {32{1'b1}};  // XOR_Gate xor_3, 32 bits wide
  Adder #(.width(32)) adder_2 (.a(xor_2_out), .b(32'h1), .out(adder_2_out));  // open: cin, cout
  Adder #(.width(32)) adder_3 (.a(xor_3_out), .b(32'h1), .out(adder_3_out));  // open: cin, cout
  Adder #(.width(16)) adder_4 (.a(A[31:16]), .b(B[31:16]), .out(vaddh[31:16]));  // open: cin, cout
  Adder #(.width(16)) adder_5 (.a(A[15:0]), .b(B[15:0]), .out(vaddh[15:0]));  // open: cin, cout
  Multiplexer #(.width(32), .enable("false")) multiplexer_2 (
    .in0(A), .in1(adder_2_out), .out(multiplexer_2_out), .sel(A[31]));
  Multiplexer #(.width(32), .enable("false")) multiplexer_3 (
    .in0(B), .in1(adder_3_out), .out(multiplexer_3_out), .sel(B[31]));
  Multiplier #(.width(32)) multiplier_4 (
    .a(multiplexer_2_out), .b(multiplexer_3_out), .cout(multiplier_4_cout));  // open: out, cin
  xor xor_4 (xor_4_out, A[31], B[31]);
  assign xor_5_out = multiplier_4_cout ^ {32{1'b1}};  // XOR_Gate xor_5, 32 bits wide
  Multiplexer #(.width(32), .enable("false")) multiplexer_4 (
    .in0(multiplier_4_cout), .in1(xor_5_out), .out(mulh), .sel(xor_4_out));

  // Other names for the same wires on the sheet: bsel[31:0] = B

  // Notes on the sheet:
  //   INPUTS to your circuit
  //   DON'T CHANGE THE LOCATIONS OF THE INPUTS AND OUTPUTS!
  //   OUTPUT from your circuit
endmodule
