// Logisim project cpu.circ as structural Verilog: 12 circuits, main circuit main
module main (
  input  [31:0] INSTRUCTION,
  input  CLOCK,
  output [31:0] FETCH_ADDRESS,
  output [31:0] ra,
  output [31:0] sp,
  output [31:0] t0,
  output [31:0] t1,
  output [31:0] t2,
  output [31:0] s0,
  output [31:0] s1,
  output [31:0] a0
);

  wire aSelO, branchcomp_1_breq, branchcomp_1_brlt, brun_1_out_2, bSelO, DMEM_p1, DMEM_p2, DMEM_p8, DMEM_p10,
       MemRWO, pcSelO, RegWEnO;
  wire [1:0] WBSelO;
  wire [3:0] aluSelO;
  wire [31:0] adder_1_out, aluO, DMEM_p11, immsel_1_out_2, INSTRUCTION1, multiplexer_1_out,
       multiplexer_2_out, multiplexer_3_out, multiplexer_4_out, Pipe, rs1, rs2, WB1;

  Adder #(.width(32)) adder_1 (.a(FETCH_ADDRESS), .b(32'h4), .out(adder_1_out));  // open: cin, cout
  BrUn brun_1 (.in_1(INSTRUCTION1), .out_2(brun_1_out_2));
  Register #(.width(32)) PC (.D(multiplexer_1_out), .clk(CLOCK), .Q(FETCH_ADDRESS));  // open: en, clr
  Multiplexer #(.width(32), .enable("false")) multiplexer_1 (
    .in0(adder_1_out), .in1(aluO), .out(multiplexer_1_out), .sel(pcSelO));
  BranchComp branchcomp_1 (
    .rs1(rs1), .rs2(rs2), .BrUn(brun_1_out_2), .BrEq(branchcomp_1_breq), .BrLt(branchcomp_1_brlt));
  Register #(.width(32)) register_1 (.D(FETCH_ADDRESS), .clk(CLOCK), .Q(Pipe));  // open: en, clr
  control control_1 (
    .BrLt(branchcomp_1_brlt), .BrEq(branchcomp_1_breq), .Inst(INSTRUCTION1), .PCSel_o(pcSelO),
    .RegWEn_o(RegWEnO), .aSel_o(aSelO), .bSel_o(bSelO), .WBSel_o(WBSelO), .MemRW_o(MemRWO), .aluSel_o(aluSelO));
  regfile_main RegFile (
    .rs2(INSTRUCTION1[24:20]), .rd(INSTRUCTION1[11:7]), .Read_Data_1(rs1), .Read_Data_2(rs2), .ra(ra),
    .sp(sp), .t0(t0), .t1(t1), .t2(t2), .s0(s0), .s1(s1), .a0(a0), .rs1(INSTRUCTION1[19:15]),
    .Write_Data(WB1), .RegWEn(RegWEnO), .clk(CLOCK));
  ImmSel immsel_1 (.in_1(INSTRUCTION1), .out_2(immsel_1_out_2));
  Multiplexer #(.width(32), .enable("false")) multiplexer_2 (
    .in0(INSTRUCTION), .in1(32'h13), .out(multiplexer_2_out), .sel(pcSelO));
  Multiplexer #(.width(32), .enable("false")) multiplexer_3 (
    .in0(Pipe), .in1(rs1), .out(multiplexer_3_out), .sel(aSelO));
  Multiplexer #(.width(32), .enable("false")) multiplexer_4 (
    .in0(rs2), .in1(immsel_1_out_2), .out(multiplexer_4_out), .sel(bSelO));
  Register #(.width(32)) register_2 (.D(multiplexer_2_out), .clk(CLOCK), .Q(INSTRUCTION1));  // open: en, clr
  alu Arithmetic_Logic_Unit (.A(multiplexer_3_out), .B(multiplexer_4_out), .ALUSel(aluSelO), .Result(aluO));
  // mem_main DMEM: pin names not known; wires that end beside it: DMEM_p1, DMEM_p2, aluO, rs2, MemRWO, CLOCK, DMEM_p2, DMEM_p8, DMEM_p8, DMEM_p10, DMEM_p11
  Multiplexer #(.select(2), .width(32), .enable("false")) multiplexer_5 (
    .in0(DMEM_p11), .in1(aluO), .in2(FETCH_ADDRESS), .out(WB1), .sel(WBSelO));  // open: in3

  // Other names for the same wires on the sheet: clk = CLOCK; rwO[4:0] = INSTRUCTION1[11:7];
  //   rr1O[4:0] = INSTRUCTION1[19:15]; rr2O[4:0] = INSTRUCTION1[24:20]; PC4[31:0] = FETCH_ADDRESS;
  //   PROGRAM_COUNTER[31:0] = FETCH_ADDRESS

  // Notes on the sheet:
  //   Output
  //   Inputs/Outputs from run.circ. DO NOT MOVE THESE.
  //   Inputs
  //   Inputs/Outputs from run.circ. DO NOT MOVE THESE.
endmodule

module PCSel (
  input  [31:0] in_1,
  input  BrLt,
  input  BrEq,
  output out_4
);

  wire and_1_out, and_2_out, and_3_out, and_4_out, and_5_out, beq, blt, bltu, bne, comparator_5_eq,
       comparator_6_eq, comparator_7_eq, not_1_out, or_1_out;

  Comparator #(.width(3), .mode("unsigned")) comparator_1 (.a(in_1[14:12]), .b(3'b000), .eq(beq));  // open: gt, lt
  Comparator #(.width(3), .mode("unsigned")) comparator_2 (.a(in_1[14:12]), .b(3'b001), .eq(bne));  // open: gt, lt
  Comparator #(.width(3), .mode("unsigned")) comparator_3 (.a(in_1[14:12]), .b(3'b100), .eq(blt));  // open: gt, lt
  Comparator #(.width(3), .mode("unsigned")) comparator_4 (.a(in_1[14:12]), .b(3'b110), .eq(bltu));  // open: gt, lt
  Comparator #(.width(7), .mode("unsigned")) comparator_5 (
    .a(in_1[6:0]), .b(7'b1100111), .eq(comparator_5_eq));  // open: gt, lt
  Comparator #(.width(7), .mode("unsigned")) comparator_6 (
    .a(in_1[6:0]), .b(7'b1101111), .eq(comparator_6_eq));  // open: gt, lt
  not not_1 (not_1_out, BrEq);
  Comparator #(.width(7), .mode("unsigned")) comparator_7 (
    .a(in_1[6:0]), .b(7'b1100011), .eq(comparator_7_eq));  // open: gt, lt
  and and_1 (and_1_out, not_1_out, bne);
  and and_2 (and_2_out, BrLt, blt);
  and and_3 (and_3_out, bltu, BrLt);
  and and_4 (and_4_out, beq, BrEq);
  and and_5 (and_5_out, comparator_7_eq, or_1_out);
  or or_1 (or_1_out, and_1_out, and_2_out, and_3_out, and_4_out);
  or or_2 (out_4, comparator_5_eq, comparator_6_eq, and_5_out);

  // Other names for the same wires on the sheet: OPCODE[6:0] = in_1[6:0]; FUNCT3[2:0] = in_1[14:12]
endmodule

module ImmSel (
  input  [31:0] in_1,
  output [31:0] out_2
);

  wire [31:0] bType, iType, jType, sType;

  assign iType = {{20{in_1[31]}}, in_1[31:20]};  // Bit_Extender bit_extender_1
  assign sType = {{20{in_1[31]}}, {in_1[31:25], in_1[11:7]}};  // Bit_Extender bit_extender_2
  assign bType = {{19{in_1[31]}}, {in_1[31], in_1[7], in_1[30:25], in_1[11:8], 1'b0}};  // Bit_Extender bit_extender_3
  assign jType = {{11{in_1[31]}}, {in_1[31], in_1[19:12], in_1[20], in_1[30:21], 1'b0}};  // Bit_Extender bit_extender_4
  Multiplexer #(.select(5), .width(32), .enable("false")) multiplexer_1 (
    .in0(iType), .in4(iType), .in8(sType), .in13({in_1[31:12], {12{1'b0}}}), .in24(bType), .in25(iType),
    .in27(jType), .out(out_2), .sel(in_1[6:2]));  // open: in1, in2, in3, in5, in6, in7, in9, in10, in11, in12, in14, in15, in16, in17, in18, in19, in20, in21, in22, in23, in26, in28, in29, in30, in31

  // Other names for the same wires on the sheet: uType[31:12] = in_1[31:12]
endmodule

module aluSel (
  input  [31:0] in_1,
  output [3:0] out_2
);

  wire comparator_1_eq, comparator_2_eq, comparator_3_eq, comparator_4_eq, comparator_5_eq, comparator_6_eq,
       comparator_7_eq, comparator_8_eq, or_1_out, vadSel;
  wire [3:0] addimul, addisub, andiremu, multiplexer_5_out, multiplexer_6_out;
  wire [4:0] selBit;

  Comparator #(.width(7), .mode("unsigned")) comparator_1 (
    .a(in_1[6:0]), .b(7'b1100011), .eq(comparator_1_eq));  // open: gt, lt
  Comparator #(.width(7), .mode("unsigned")) comparator_2 (
    .a(in_1[6:0]), .b(7'b1100111), .eq(comparator_2_eq));  // open: gt, lt
  Comparator #(.width(7), .mode("unsigned")) comparator_3 (
    .a(in_1[6:0]), .b(7'b1101111), .eq(comparator_3_eq));  // open: gt, lt
  Comparator #(.width(7), .mode("unsigned")) comparator_4 (
    .a(in_1[6:0]), .b(7'b0100011), .eq(comparator_4_eq));  // open: gt, lt
  Comparator #(.width(7), .mode("unsigned")) comparator_5 (
    .a(in_1[6:0]), .b(7'b0000011), .eq(comparator_5_eq));  // open: gt, lt
  Multiplexer #(.width(4), .enable("false")) multiplexer_1 (
    .in0(4'b0001), .in1(4'b1001), .out(andiremu), .sel(in_1[5]));
  Multiplexer #(.width(4), .enable("false")) multiplexer_2 (.in0(4'b0000), .in1(4'b1100), .out(addisub), .sel(in_1[5]));
  Multiplexer #(.width(4), .enable("false")) multiplexer_3 (.in0(4'b0000), .in1(4'b1010), .out(addimul), .sel(in_1[5]));
  or or_1 (or_1_out, comparator_1_eq, comparator_2_eq, comparator_3_eq, comparator_4_eq, comparator_5_eq);
  Multiplexer #(.width(5), .enable("false")) multiplexer_4 (
    .in0({in_1[14:12], in_1[30], in_1[25]}), .in1({5{1'b0}}), .out(selBit), .sel(or_1_out));
  Multiplexer #(.select(5), .width(4), .enable("false")) multiplexer_5 (
    .in0(4'b0000), .in1(addimul), .in2(addisub), .in3(4'b0000), .in4(4'b0110), .in5(4'b1110), .in8(4'b0111),
    .in9(4'b0111), .in10(4'b0111), .in11(4'b0111), .in13(4'b1011), .in16(4'b0011), .in17(4'b0011),
    .in18(4'b0011), .in19(4'b0011), .in20(4'b0100), .in21(4'b1000), .in22(4'b0101), .in24(4'b0010),
    .in25(4'b0010), .in26(4'b0010), .in27(4'b0010), .in28(4'b0001), .in29(andiremu), .in30(4'b0001),
    .in31(4'b0001), .out(multiplexer_5_out), .sel(selBit));  // open: in6, in7, in12, in14, in15, in23
  Comparator #(.width(7)) comparator_6 (.a(in_1[31:25]), .b(7'b0001111), .eq(comparator_6_eq));  // open: gt, lt
  Comparator #(.width(3)) comparator_7 (.a(in_1[14:12]), .b(3'b000), .eq(comparator_7_eq));  // open: gt, lt
  Multiplexer #(.width(4), .enable("false")) multiplexer_6 (
    .in0(multiplexer_5_out), .in1(4'b1101), .out(multiplexer_6_out), .sel(comparator_8_eq));
  Comparator #(.width(7)) comparator_8 (.a(in_1[6:0]), .b(7'b0110111), .eq(comparator_8_eq));  // open: gt, lt
  Multiplexer #(.width(4), .enable("false")) multiplexer_7 (
    .in0(multiplexer_6_out), .in1(4'b1111), .out(out_2), .sel(vadSel));
  and and_1 (vadSel, comparator_6_eq, comparator_7_eq);

  // Other names for the same wires on the sheet: FUNCT7[6:0] = in_1[31:25]; FUNCT7_2bit[1:0] = {in_1[30], in_1[25]};
  //   FUNCT3[2:0] = in_1[14:12]; OPCODE[6:0] = in_1[6:0]; OPCODE5 = in_1[5]

  // Notes on the sheet:
  //   andi
  //   remu
  //   addi
  //   sub
  //   addi
  //   mul
  //   srls
  //   sras
  //   adds
  //   slls
  //   slts
  //   xor
  //   divu
  //   mulh
  //   mulhu
  //   ors
  //   ands
  //   lui
endmodule

module BSel (
  input  [31:0] in_1,
  output out_2
);

  wire comparator_1_eq;

  Comparator #(.width(7), .mode("unsigned")) comparator_1 (
    .a(in_1[6:0]), .b(7'b0110011), .eq(comparator_1_eq));  // open: gt, lt
  not not_1 (out_2, comparator_1_eq);
endmodule

module WBSel (
  input  [31:0] in_1,
  output [1:0] out_2
);

  Multiplexer #(.select(5), .width(2), .enable("false")) multiplexer_1 (
    .in0(2'b00), .in4(2'b01), .in8(2'b00), .in12(2'b01), .in13(2'b01), .in24(2'b00), .in25(2'b10),
    .in27(2'b10), .out(out_2), .sel(in_1[6:2]));  // open: in1, in2, in3, in5, in6, in7, in9, in10, in11, in14, in15, in16, in17, in18, in19, in20, in21, in22, in23, in26, in28, in29, in30, in31

  // Other names for the same wires on the sheet: OPCODE[6:0] = in_1[6:0]; OPCODE5[4:0] = in_1[6:2]

  // Notes on the sheet:
  //   pc4
  //   mem
  //   pc4
  //   alu
  //   pc4
  //   alu
endmodule

module MemRW (
  input  [31:0] in_1,
  output out_2
);

  Comparator #(.width(7), .mode("unsigned")) comparator_1 (.a(in_1[6:0]), .b(7'b0100011), .eq(out_2));  // open: gt, lt
endmodule

module ASel (
  input  [31:0] in_1,
  output out_2
);

  wire comparator_1_eq, comparator_2_eq, not_1_out, or_1_out;

  Comparator #(.width(7), .mode("unsigned")) comparator_1 (
    .a(in_1[6:0]), .b(7'b1100011), .eq(comparator_1_eq));  // open: gt, lt
  Comparator #(.width(7), .mode("unsigned")) comparator_2 (
    .a(in_1[6:0]), .b(7'b1101111), .eq(comparator_2_eq));  // open: gt, lt
  or or_1 (or_1_out, comparator_1_eq, comparator_2_eq);
  not not_1 (not_1_out, or_1_out);
  Multiplexer #(.enable("false")) multiplexer_1 (.in0(1'b0), .in1(1'b1), .out(out_2), .sel(not_1_out));

  // Other names for the same wires on the sheet: OPCODE[6:0] = in_1[6:0]; FUNCT3[2:0] = in_1[14:12]
endmodule

module control (
  input  BrLt,
  input  BrEq,
  input  [31:0] Inst,
  output PCSel_o,
  output RegWEn_o,
  output aSel_o,
  output bSel_o,
  output [1:0] WBSel_o,
  output MemRW_o,
  output [3:0] aluSel_o
);

  ASel asel_1 (.in_1(Inst), .out_2(aSel_o));
  BSel bsel_1 (.in_1(Inst), .out_2(bSel_o));
  WBSel wbsel_1 (.in_1(Inst), .out_2(WBSel_o));
  MemRW memrw_1 (.in_1(Inst), .out_2(MemRW_o));
  PCSel pcsel_1 (.in_1(Inst), .BrLt(BrLt), .BrEq(BrEq), .out_4(PCSel_o));
  RegWEn regwen_1 (.in_1(Inst), .out_2(RegWEn_o));
  aluSel alusel_1 (.in_1(Inst), .out_2(aluSel_o));
endmodule

module RegWEn (
  input  [31:0] in_1,
  output out_2
);

  wire comparator_1_eq, comparator_2_eq, or_1_out;

  Comparator #(.width(7), .mode("unsigned")) comparator_1 (
    .a(in_1[6:0]), .b(7'b1100011), .eq(comparator_1_eq));  // open: gt, lt
  Comparator #(.width(7), .mode("unsigned")) comparator_2 (
    .a(in_1[6:0]), .b(7'b0100011), .eq(comparator_2_eq));  // open: gt, lt
  or or_1 (or_1_out, comparator_1_eq, comparator_2_eq);
  not not_1 (out_2, or_1_out);

  // Other names for the same wires on the sheet: OPCODE[6:0] = in_1[6:0]
endmodule

module BrUn (
  input  [31:0] in_1,
  output out_2
);

  wire comparator_1_eq;

  Comparator #(.width(7), .mode("unsigned")) comparator_1 (
    .a(in_1[6:0]), .b(7'b1100011), .eq(comparator_1_eq));  // open: gt, lt
  and and_1 (out_2, comparator_1_eq, in_1[13]);
endmodule

module BranchComp (
  input  [31:0] rs1,
  input  [31:0] rs2,
  input  BrUn,
  output BrEq,
  output BrLt
);

  wire comparator_1_lt, comparator_2_lt;

  Comparator #(.width(32)) comparator_1 (.a(rs1), .b(rs2), .eq(BrEq), .lt(comparator_1_lt));  // open: gt
  Comparator #(.width(32), .mode("unsigned")) comparator_2 (.a(rs1), .b(rs2), .lt(comparator_2_lt));  // open: gt, eq
  Multiplexer #(.enable("false")) multiplexer_1 (.in0(comparator_1_lt), .in1(comparator_2_lt), .out(BrLt), .sel(BrUn));
endmodule
