// Logisim project regfile.circ as structural Verilog: 1 circuit, main circuit main
module main (
  input  [4:0] rs1,
  input  [4:0] rs2,
  input  [4:0] rd,
  input  [31:0] Write_Data,
  input  RegWEn,
  input  clk,
  output [31:0] ra,
  output [31:0] sp,
  output [31:0] t0,
  output [31:0] t1,
  output [31:0] t2,
  output [31:0] s0,
  output [31:0] s1,
  output [31:0] a0,
  output [31:0] Read_Data_1,
  output [31:0] Read_Data_2
);

  wire x0w, x1w, x2w, x5w, x6w, x7w, x8w, x9w, x10w;
  wire [31:0] x0;

  Register #(.width(32)) x6 (.D(Write_Data), .en(x6w), .clk(clk), .Q(t1));  // open: clr
  Register #(.width(32)) x10 (.D(Write_Data), .en(x10w), .clk(clk), .Q(a0));  // open: clr
  Register #(.width(32)) u_x0 (.D({32{1'b0}}), .en(x0w), .clk(clk), .Q(x0));  // open: clr
  Demultiplexer #(.select(5), .enable("false")) demultiplexer_1 (
    .out0(x0w), .out1(x1w), .out2(x2w), .out5(x5w), .out6(x6w), .out7(x7w), .out8(x8w), .out9(x9w),
    .out10(x10w), .in(RegWEn), .sel(rd));  // open: out3, out4, out11, out12, out13, out14, out15, out16, out17, out18, out19, out20, out21, out22, out23, out24, out25, out26, out27, out28, out29, out30, out31
  Register #(.width(32)) x1 (.D(Write_Data), .en(x1w), .clk(clk), .Q(ra));  // open: clr
  Register #(.width(32)) x7 (.D(Write_Data), .en(x7w), .clk(clk), .Q(t2));  // open: clr
  Multiplexer #(.select(5), .width(32), .enable("false")) multiplexer_1 (
    .in0(x0), .in1(ra), .in2(sp), .in5(t0), .in6(t1), .in7(t2), .in8(s0), .in9(s1), .in10(a0),
    .out(Read_Data_1), .sel(rs1));  // open: in3, in4, in11, in12, in13, in14, in15, in16, in17, in18, in19, in20, in21, in22, in23, in24, in25, in26, in27, in28, in29, in30, in31
  Register #(.width(32)) x2 (.D(Write_Data), .en(x2w), .clk(clk), .Q(sp));  // open: clr
  Register #(.width(32)) x8 (.D(Write_Data), .en(x8w), .clk(clk), .Q(s0));  // open: clr
  Multiplexer #(.select(5), .width(32), .enable("false")) multiplexer_2 (
    .in0(x0), .in1(ra), .in2(sp), .in5(t0), .in6(t1), .in7(t2), .in8(s0), .in9(s1), .in10(a0),
    .out(Read_Data_2), .sel(rs2));  // open: in3, in4, in11, in12, in13, in14, in15, in16, in17, in18, in19, in20, in21, in22, in23, in24, in25, in26, in27, in28, in29, in30, in31
  Register #(.width(32)) x5 (.D(Write_Data), .en(x5w), .clk(clk), .Q(t0));  // open: clr
  Register #(.width(32)) x9 (.D(Write_Data), .en(x9w), .clk(clk), .Q(s1));  // open: clr

  // Other names for the same wires on the sheet: read_data1[31:0] = Read_Data_1; read_data2[31:0] = Read_Data_2;
  //   read_reg1[4:0] = rs1; read_reg2[4:0] = rs2; write_en = RegWEn; write_reg[4:0] = rd; x1[31:0] = ra;
  //   x2[31:0] = sp; x5[31:0] = t0; x6[31:0] = t1; x7[31:0] = t2; x8[31:0] = s0; x9[31:0] = s1; x10[31:0] = a0

  // Notes on the sheet:
  //   INPUTS to your circuit
  //   DON'T CHANGE THE LOCATIONS OF THE INPUTS AND OUTPUTS!
  //   These are DEBUG/TEST outputs from your circuit.
  //   OUTPUTS from your circuit
endmodule
